// Logisim project additionneur.circ as structural Verilog: 4 circuits, main circuit main
module main (
  input  e_1,
  input  e_0,
  output s_1,
  output r_1
);

  xor xor_1 (s_1, e_1, e_0);
  and and_1 (r_1, e_1, e_0);

  // Notes on the sheet:
  //   additionneur 1 bit
endmodule

module demi_additionneur (
  input  e_1,
  input  e_0,
  output s_1,
  output r_1
);

  xor xor_1 (s_1, e_1, e_0);
  and and_1 (r_1, e_1, e_0);

  // Notes on the sheet:
  //   additionneur 1 bit
endmodule

module additionneur1bit (
  input  in_1,
  input  in_2,
  input  in_3,
  output s_1,
  output out_5,
  output r_2,
  output r_1,
  output out_8
);

  xor xor_1 (s_1, in_2, in_3);
  and and_1 (r_1, in_2, in_3);
  xor xor_2 (out_5, in_1, s_1);
  and and_2 (r_2, in_1, s_1);
  or or_1 (out_8, r_2, r_1);

  // Notes on the sheet:
  //   Bit de retenue entrante r(0)
  //   Bit d'opérande e(1)
  //   Bit d'opérande e(0)
  //   additionneur 1 bit
  //   Bit de résultat s(2)
  //   Bit de retenue sortante r(3)
endmodule

module additionneur2bits (
  input  in_1,
  input  in_2,
  input  in_3,
  input  in_4,
  input  in_5,
  input  in_6,
  output s_1,
  output out_8,
  output r_2,
  output r_1,
  output out_11,
  output s_1_2,
  output out_13,
  output r_2_2,
  output r_1_2,
  output out_16
);

  xor xor_1 (s_1, in_2, in_3);
  and and_1 (r_1, in_2, in_3);
  xor xor_2 (s_1_2, in_5, in_6);
  and and_2 (r_1_2, in_5, in_6);
  xor xor_3 (out_8, in_1, s_1);
  and and_3 (r_2, in_1, s_1);
  xor xor_4 (out_13, in_4, s_1_2);
  and and_4 (r_2_2, in_4, s_1_2);
  or or_1 (out_11, r_2, r_1);
  or or_2 (out_16, r_2_2, r_1_2);

  // Notes on the sheet:
  //   Bit de retenue entrante r(0)
  //   Premier bit d'opérande e(1)
  //   Premier bit d'opérande e(0)
  //   Second bit  d'opérande e(1)
  //   Second bit  d'opérande e(0)
  //   additionneur 2  bits avec deux additionneurs 1bit en série
  //   Premier bit de résultat s(2)
  //   Bit de retenue sortante r(3)
  //   Second bit  de résultat s(2)
  //   Bit de retenue sortante r(3)
endmodule
