// Logisim project demi_additionneur.circ as structural Verilog: 1 circuit, main circuit main
module main (
  input  e_1,
  input  e_0,
  output s,
  output r
);

  xor xor_1 (s, e_1, e_0);
  and and_1 (r, e_1, e_0);

  // Notes on the sheet:
  //   demi-additionneur 1 bit
endmodule
