// Logisim project exercice11.circ as structural Verilog: 1 circuit, main circuit main
module main (
  input  e0,
  input  e1,
  output s_e0__e1,
  output r_e0__e1
);

  wire and_1_out, and_2_out, not_1_out, not_2_out;

  not not_1 (not_1_out, e0);
  not not_2 (not_2_out, e1);
  and and_1 (and_1_out, not_1_out, e1);
  and and_2 (and_2_out, not_2_out, e0);
  and and_3 (r_e0__e1, e1, e0);
  or or_1 (s_e0__e1, and_1_out, and_2_out);
endmodule
