// Logisim project exercice4.circ as structural Verilog: 1 circuit, main circuit main
module main (
  input  in_1,
  input  in_2,
  input  in_3,
  input  in_4,
  output out_5,
  output out_6
);

  wire nand_1_out, nor_1_out;

  nor nor_1 (nor_1_out, in_1, in_2);
  nand nand_1 (nand_1_out, in_3, in_4);
  nor nor_2 (out_5, nor_1_out, nor_1_out);
  nand nand_2 (out_6, nand_1_out, nand_1_out);
endmodule
