// Logisim project porte_NAND.circ as structural Verilog: 1 circuit, main circuit main
module main (
  input  in_1,
  input  in_2,
  output Sortie
);

  wire transistor_2_out;

  Pull_Resistor #(.pull(1)) pull_resistor_1 (.node(Sortie));
  Transistor #(.\type ("n")) transistor_1 (.in(transistor_2_out), .out(Sortie), .gate(in_1));
  Transistor #(.\type ("n")) transistor_2 (.in(1'b0), .out(transistor_2_out), .gate(in_2));

  // Notes on the sheet:
  //   Porte  NAND deux transistors en série
  //    Grille Transistor 2
  //   Grille  transistor 1
  //   Source
endmodule
