// Logisim project exercice3.circ as structural Verilog: 1 circuit, main circuit main
module main (
  input  A,
  input  A_2,
  input  B,
  output B_2,
  output C
);

  wire nor_2_out, nor_3_out;

  nor nor_1 (B_2, A, A);
  nor nor_2 (nor_2_out, A_2, A_2);
  nor nor_3 (nor_3_out, B, B);
  nor nor_4 (C, nor_2_out, nor_3_out);

  // Notes on the sheet:
  //   Exercice 2 question 2
  //   Exercice 2 question 1
endmodule
