// Logisim project porte_NOR.circ as structural Verilog: 1 circuit, main circuit main
module main (
  input  in_1,
  input  in_2,
  output Sortie
);

  Pull_Resistor #(.pull(1)) pull_resistor_1 (.node(Sortie));
  Transistor #(.\type ("n")) transistor_1 (.in(1'b0), .out(Sortie), .gate(in_1));
  Transistor #(.\type ("n")) transistor_2 (.in(1'b0), .out(Sortie), .gate(in_2));

  // Notes on the sheet:
  //   Porte NOR deux transistors en parallèles
  //    Grille Transistor 1
  //   Grille Transistor 2
  //   Source
endmodule
