// Logisim project portes_logiques_americaines.circ as structural Verilog: 1 circuit, main circuit main
module main (
);

  wire and_1_out, nand_1_out, nor_1_out, not_1_out, or_1_out, undriven, undriven_2, undriven_3, undriven_4,
       undriven_5, undriven_6, undriven_7, undriven_8, undriven_9, undriven_10, undriven_11, xor_1_out;

  and and_1 (and_1_out, undriven, undriven_2);
  nand nand_1 (nand_1_out, undriven_3, undriven_4);
  or or_1 (or_1_out, undriven_5, undriven_6);
  nor nor_1 (nor_1_out, undriven_7, undriven_8);
  not not_1 (not_1_out, undriven_11);
  xor xor_1 (xor_1_out, undriven_9, undriven_10);

  // Notes on the sheet:
  //   A
  //   B
  //   Porte AND américaine
  //   Porte NAND américaine
  //   C
  //   A
  //   B
  //   A
  //   B
  //   Porte OR américaine
  //   Porte NOR américaine
  //   C
  //   C
  //   A
  //   B
  //   Porte XOR américaine
  //   Porte  NOT américaine
  //   A
  //   C
  //   B
endmodule
