// Logisim project transistor.circ as structural Verilog: 1 circuit, main circuit main
module main (
  input  Grille,
  output Drain
);

  Pull_Resistor #(.pull(1)) pull_resistor_1 (.node(Drain));
  Transistor #(.\type ("n")) transistor_1 (.in(1'b0), .out(Drain), .gate(Grille));

  // Notes on the sheet:
  //   TRANSISTOR de type N
  //   Source
endmodule
